# Fritzing sketch servo-capacitor (saved by Fritzing 0.9.3b)
breadboards: 1

parts:
  Part1 = Arduino Uno (Rev3)
  J1 = Basic Servo
  C1 = Electrolytic Capacitor [capacitance=100μF voltage=35V package="0807 [SMD, electrolytic]"]

nets:
  N1: Part1.D9_PWM, J1.pulse
  5V: Part1.5V, J1.vcc, C1.+
  GND: Part1.GND, J1.gnd, C1.-
